# Fritzing sketch ap (saved by Fritzing 0.9.4)
breadboards: 1

parts:
  CUI-enc1 = AMT103
  D1 = Rectifier Diode 10A [part_number=P1000K]
  R1 = Resistor [tolerance=±5% resistance=100 package="2512 [SMD]"]
  R2 = Resistor [tolerance=±5% resistance=100 package="2512 [SMD]"]
  D2 = Rectifier Diode 10A [part_number=P1000K]
  C1 = Ceramic Capacitor [capacitance="100 nF" package="0603 [SMD, multilayer]"]
  C2 = Ceramic Capacitor [capacitance=100nF voltage=6.3V part_number=104 package="0603 [SMD, multilayer]"]
  S3 = Square Pushbutton
  R3 = Resistor [tolerance=±5% resistance=10 package="2512 [SMD]"]
  LED1 = RGB LED - (4 legs) [package="5 mm [THT]"]
  R4 = Resistor [tolerance=±5% resistance=220 package="2512 [SMD]"]
  R5 = Resistor [tolerance=±5% resistance=220 package="2512 [SMD]"]
  R6 = Resistor [tolerance=±5% resistance=220 package="2512 [SMD]"]

nets:
  N1: CUI-enc1.B, C1.1, C2.1, S3.leg1, R3.Pin_1
  N2: CUI-enc1.5V, LED1.common_anode
  N3: CUI-enc1.X, R1.Pin_0
  N4: CUI-enc1.GND, R2.Pin_0
  N5: D1.anode, R1.Pin_1, C1.0
  N6: R2.Pin_1, D2.anode, C2.0
  N7: S3.leg0, R3.Pin_0
  N8: LED1.red_cathode, R4.Pin_0
  N9: LED1.green_cathode, R5.Pin_0
  N10: LED1.blue_cathode, R6.Pin_0

notes:
  G01234567890V456789012
  N 13222222333
  D 3
  Teensy 3.6
  VG32109876543G...9876543
  IN22221111111N...3333333
  ND
  // pins for the rotary encoders
  #define R1_1 24 // BARO
  #define R1_2 25
  #define R2_1 26 // CRS
  #define R2_2 27
  #define R3_1 28 // HDG
  #define R3_2 29
  #define R4_1 30 // SPD
  #define R4_2 31
  #define R5_1 14 // ALT
  #define R5_2 15
  #define R6_1 16 // VS
  #define R6_2 17
  #define INTERNAL_LED 13
  #define LED_RED 33
  #define LED_GREEN 34
  #define LED_BLUE 35
  // pins for the buttons
  const int BTN[12] = {
  0, // BARO RE
  1, // CRS RE
  2, // HDG RE
  3, // ALT RE
  4, // VS
  5, // VNAV
  6, // FLC
  7, // AP
  8, // NAV
  9, // HDG
  10, // APPR
  11, // ALT
  };
  6x
  8x
